# Fritzing sketch 01-pwmLED (saved by Fritzing 0.9.3b)
breadboards: 1

parts:
  LED1 = LED - 5mm [color="Blue (470nm)" package="5 mm [THT]"]
  R1 = Resistor [tolerance=±5% resistance=220 package=THT]
  Part1 = Adafruit Feather HUZZAH ESP8266 [part_number="Adafruit #2821"]

nets:
  N1: LED1.cathode, R1.Pin_0
  N2: LED1.anode, Part1.GPIO14/SCK
  N3: R1.Pin_1, Part1.GND

custom parts:
  Adafruit Feather HUZZAH ESP8266: his is the Adafruit Feather HUZZAH ESP8266 - our take on an 'all-in-one' ESP8266 WiFi development board with built in USB and battery charging. Its an ESP8266 WiFi module with all the extras you need, ready to rock! We have other boards in the Feather family, check'em out here. At the Feather HUZZAH's heart is an ESP8266 WiFi microcontroller clocked at 80 MHz and at 3.3V logic. This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

// code stored in the sketch: 01-pwmLED.ino

