# Fritzing sketch 03-analogRead (saved by Fritzing 0.9.3b)
breadboards: 1

parts:
  Part1 = Arduino Micro (Rev3)
  LED1 = LED - 5mm [color="Blue (470nm)" package="5 mm [THT]"]
  R1 = Resistor [tolerance=±5% resistance=220 package=THT]
  R3 = Rotary Potentiometer (Small) [maximum_resistance=100kΩ package=THT]

nets:
  N1: Part1.D11_PWM, LED1.anode
  N2: Part1.GND, R1.Pin_1, R3.leg2
  N3: Part1.5V, R3.leg1
  N4: Part1.A1, R3.wiper
  N5: LED1.cathode, R1.Pin_0

// code stored in the sketch: 01-pwmLED.ino

