# Fritzing sketch 04-photoSensor (saved by Fritzing 0.9.3b)
breadboards: 1

parts:
  R2 = Photocell (LDR) [package=THT]
  Part1 = Adafruit Feather HUZZAH ESP8266 [part_number="Adafruit #2821"]
  R3 = Resistor [tolerance=±5% resistance=39 package=THT]
  J1 = Piezo Speaker

nets:
  N1: R2.pin_0, Part1.ADC, R3.Pin_1
  N2: R2.pin_1, Part1.3.3V
  N3: Part1.GPIO14/SCK, J1.pin2
  GND: Part1.GND, R3.Pin_0, J1.pin1

custom parts:
  Adafruit Feather HUZZAH ESP8266: his is the Adafruit Feather HUZZAH ESP8266 - our take on an 'all-in-one' ESP8266 WiFi development board with built in USB and battery charging. Its an ESP8266 WiFi module with all the extras you need, ready to rock! We have other boards in the Feather family, check'em out here. At the Feather HUZZAH's heart is an ESP8266 WiFi microcontroller clocked at 80 MHz and at 3.3V logic. This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

// code stored in the sketch: 01-pwmLED.ino

