# Fritzing sketch 04-photosensor (saved by Fritzing 0.9.3b)
breadboards: 1

parts:
  Part1 = Arduino Micro (Rev3)
  LED1 = LED - 5mm [color="Blue (470nm)" package="5 mm [THT]"]
  R1 = Resistor [tolerance=±5% resistance=220 package=THT]
  LED2 = LED - 5mm [color="Red (633nm)" package="5 mm [THT]"]
  R2 = Resistor [tolerance=±5% resistance=220 package=THT]

nets:
  N1: Part1.D11_PWM, LED1.anode
  N2: Part1.GND, R1.Pin_1, LED2.cathode
  N3: Part1.5V, R2.Pin_0
  N4: LED1.cathode, R1.Pin_0
  N5: LED2.anode, R2.Pin_1

// code stored in the sketch: 01-pwmLED.ino

