# Fritzing sketch 05-servos (saved by Fritzing 0.9.3b)
breadboards: 1

parts:
  Part1 = Adafruit Feather HUZZAH ESP8266 [part_number="Adafruit #2821"]
  S2 = Pushbutton [package="[THT]"]
  S1 = Pushbutton [package="[THT]"]
  J1 = Basic Servo

nets:
  N1: Part1.GPIO12/MISO, S1.Pin_3, S1.Pin_4
  N2: Part1.GPIO13/MOSI, S2.Pin_3, S2.Pin_4
  N3: Part1.GPIO14/SCK, J1.pulse
  GND: Part1.GND, S2.Pin_1, S2.Pin_2, S1.Pin_1, S1.Pin_2, J1.gnd
  N4: Part1.VBUS, J1.vcc

custom parts:
  Adafruit Feather HUZZAH ESP8266: his is the Adafruit Feather HUZZAH ESP8266 - our take on an 'all-in-one' ESP8266 WiFi development board with built in USB and battery charging. Its an ESP8266 WiFi module with all the extras you need, ready to rock! We have other boards in the Feather family, check'em out here. At the Feather HUZZAH's heart is an ESP8266 WiFi microcontroller clocked at 80 MHz and at 3.3V logic. This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

// code stored in the sketch: 01-pwmLED.ino

